# Fritzing sketch rocket_sensors_rev1 (saved by Fritzing 0.9.3b)
breadboards: 1

parts:
  Part1 = Arduino Uno (Rev3)
  part = Resistor [tolerance=±5% resistance=10k package=THT]
  Part2 = Arduino MicroSD Shield
  part_2 = Temperature Sensor (Thermistor) [thermistor_type=NTC part_number=NTCLE100E3103HT1 package=THT]
  Part3 = 9 Degrees of Freedom - Sensor Stick
  47pF = Capacitor [package=cap-pth-5mm]
  part_3 = Resistor [tolerance=±5% resistance=51k package=THT]
  100nF = Capacitor [package=cap-pth-small-kit]
  part_4 = Resistor [tolerance=±5% resistance=51k package=THT]
  47pF_2 = Capacitor [package=cap-pth-5mm]
  100nF_2 = Capacitor [package=cap-pth-small-kit]
  IC1 = DIP - 8 pins [chip_label=MP3H6115A6U package="DIP (Dual Inline) [THT]"]
  SSCDLNN100PGAA1 = SSCDLNN100PGAA5 [chip_label=SSCDLNN100PGAA5 package="DIP (Dual Inline) [THT]"]
  IC2 = DIP - 8 pins [chip_label=MP3H6115A6U package="DIP (Dual Inline) [THT]"]
  part_5 = Resistor [tolerance=±5% resistance=10k package=THT]
  part_6 = Resistor [tolerance=±5% resistance=10k package=THT]
  J1 = Basic Servo

nets:
  N1: Part1.A0, part_5.Pin_1, part_6.Pin_0
  N2: Part1.A1, 47pF.2, part_3.Pin_1, IC2.pin4
  N3: Part1.A2, part_4.Pin_1, 47pF_2.2, IC1.pin4
  N4: Part1.A3, part.Pin_1, part_2.pin_0
  N5: Part1.A4/SDA, Part3.SDA
  N6: Part1.A5/SCL, Part3.SCL
  N7: Part1.D8, Part2.CS
  N8: Part1.D11_PWM/MOSI, Part2.MOSI
  N9: Part1.D12/MISO, Part2.MISO
  N10: Part1.D13/SCK, Part2.SCK
  GND: Part1.GND, part_2.pin_1, Part3.GND, 47pF.1, 100nF.2, part_4.Pin_0, 47pF_2.1, 100nF_2.2, IC1.pin3, SSCDLNN100PGAA1.Vout, IC2.pin3, part_6.Pin_1, J1.gnd
  N11: Part1.AREF, Part1.3V3
  N12: Part1.D3_PWM, J1.pulse
  5V: Part1.5V, SSCDLNN100PGAA1.Vs, J1.vcc
  3.3V: part.Pin_0, Part3.VCC, 100nF.1, 100nF_2.1, IC1.pin2, IC2.pin2
  N13: SSCDLNN100PGAA1.GND, part_5.Pin_0

custom parts:
  DIP - 8 pins: A DIP stand-in part for whatever IC you want. With 8 pins on a 300mil dual inline package (DIP) footprint.
